// Logisim project examples.circ as structural Verilog
module bus_and_rgisters (
  input  in_1,
  input  in_2,
  input  in_3,
  input  in_4,
  input  in_5,
  input  in_6,
  input  in_7,
  input  in_8,
  input  in_9,
  input  in_10,
  input  in_11,
  output out_12,
  output out_13,
  output out_14,
  output out_15,
  output out_16,
  output out_17,
  output out_18,
  output out_19,
  output out_20,
  output out_21
);

  wire clock_1_out, j_k_ff_1_q, j_k_ff_2_q, j_k_ff_3_q, j_k_ff_4_q, j_k_ff_5_q, j_k_ff_6_q, j_k_ff_7_q,
       j_k_ff_8_q;
  wire [7:0] j_k_ff_1_qn;

  Clock clock_1 (.out(clock_1_out));
  J_K_Flip_Flop j_k_ff_1 (
    .J(clock_1_out), .K(clock_1_out), .clk(clock_1_out), .Q(j_k_ff_1_q), .Qn(j_k_ff_1_qn[0]), .reset(in_7));  // open: preset
  J_K_Flip_Flop j_k_ff_2 (
    .J(j_k_ff_1_q), .K(j_k_ff_1_q), .clk(j_k_ff_1_q), .Q(j_k_ff_2_q), .Qn(j_k_ff_1_qn[1]), .reset(in_7));  // open: preset
  J_K_Flip_Flop j_k_ff_3 (
    .J(j_k_ff_2_q), .K(j_k_ff_2_q), .clk(j_k_ff_2_q), .Q(j_k_ff_3_q), .Qn(j_k_ff_1_qn[2]), .reset(in_7));  // open: preset
  J_K_Flip_Flop j_k_ff_4 (
    .J(j_k_ff_3_q), .K(j_k_ff_3_q), .clk(j_k_ff_3_q), .Q(j_k_ff_4_q), .Qn(j_k_ff_1_qn[3]), .reset(in_7));  // open: preset
  J_K_Flip_Flop j_k_ff_5 (
    .J(j_k_ff_4_q), .K(j_k_ff_4_q), .clk(j_k_ff_4_q), .Q(j_k_ff_5_q), .Qn(j_k_ff_1_qn[4]), .reset(in_7));  // open: preset
  J_K_Flip_Flop j_k_ff_6 (
    .J(j_k_ff_5_q), .K(j_k_ff_5_q), .clk(j_k_ff_5_q), .Q(j_k_ff_6_q), .Qn(j_k_ff_1_qn[5]), .reset(in_7));  // open: preset
  J_K_Flip_Flop j_k_ff_7 (
    .J(j_k_ff_6_q), .K(j_k_ff_6_q), .clk(j_k_ff_6_q), .Q(j_k_ff_7_q), .Qn(j_k_ff_1_qn[6]), .reset(in_7));  // open: preset
  J_K_Flip_Flop j_k_ff_8 (
    .J(j_k_ff_7_q), .K(j_k_ff_7_q), .clk(j_k_ff_7_q), .Q(j_k_ff_8_q), .Qn(j_k_ff_1_qn[7]), .reset(in_7));  // open: preset
  ROM rom_1 ();  // open: addr, data
  RAM ram_1 (.addr(j_k_ff_1_qn));  // open: we, oe, clk, din, dout
  Adder adder_1 (
    .a(j_k_ff_1_qn), .b(j_k_ff_1_qn), .out({out_21, out_20, out_19, out_18, out_17, out_16, out_15, out_14}));  // open: cin, cout
  T_Flip_Flop t_ff_1 ();  // open: T, clk, Q, Qn, reset, preset
  D_Flip_Flop d_ff_1 ();  // open: D, clk, Q, Qn, preset, reset
  J_K_Flip_Flop j_k_ff_9 (.J(in_2), .K(in_3), .clk(in_4), .Q(out_12), .Qn(out_13), .preset(in_1), .reset(in_5));
  S_R_Flip_Flop s_r_ff_1 (.S(in_8), .R(in_9), .clk(in_10), .reset(in_11), .preset(in_6));  // open: Q, Qn
endmodule

module counterr (
  input  in_1
);

  wire clock_1_out, j_k_ff_1_q, j_k_ff_2_q, j_k_ff_3_q, j_k_ff_4_q;
  wire [3:0] j_k_ff_1_qn;

  Clock clock_1 (.out(clock_1_out));
  J_K_Flip_Flop j_k_ff_1 (
    .J(clock_1_out), .K(clock_1_out), .clk(clock_1_out), .Q(j_k_ff_1_q), .Qn(j_k_ff_1_qn[0]), .reset(in_1));  // open: preset
  J_K_Flip_Flop j_k_ff_2 (
    .J(j_k_ff_1_q), .K(j_k_ff_1_q), .clk(j_k_ff_1_q), .Q(j_k_ff_2_q), .Qn(j_k_ff_1_qn[1]), .reset(in_1));  // open: preset
  J_K_Flip_Flop j_k_ff_3 (
    .J(j_k_ff_2_q), .K(j_k_ff_2_q), .clk(j_k_ff_2_q), .Q(j_k_ff_3_q), .Qn(j_k_ff_1_qn[2]), .reset(in_1));  // open: preset
  J_K_Flip_Flop j_k_ff_4 (
    .J(j_k_ff_3_q), .K(j_k_ff_3_q), .clk(j_k_ff_3_q), .Q(j_k_ff_4_q), .Qn(j_k_ff_1_qn[3]), .reset(in_1));  // open: preset
  RAM #(.addrWidth(4), .dataWidth(4)) ram_1 (.addr(j_k_ff_1_qn));  // open: we, oe, clk, din, dout
endmodule

module registro_8bit (
  input  CLOCK,
  input  LOAD,
  input  RESET,
  input  ENABLE,
  input  I0,
  input  I1,
  input  I2,
  input  I3,
  input  I4,
  input  I5,
  input  I6,
  input  I7,
  output L0,
  output L1,
  output L2,
  output L3,
  output L4,
  output L5,
  output L6,
  output L7,
  output O0,
  output O1,
  output O2,
  output O3,
  output O4,
  output O5,
  output O6,
  output O7
);

  Register #(.width(1)) register_1 (.D(I0), .en(LOAD), .clk(CLOCK), .Q(L0), .clr(RESET));
  Register #(.width(1)) register_2 (.D(I1), .en(LOAD), .clk(CLOCK), .Q(L1), .clr(RESET));
  Register #(.width(1)) register_3 (.D(I2), .en(LOAD), .clk(CLOCK), .Q(L2), .clr(RESET));
  Register #(.width(1)) register_4 (.D(I3), .en(LOAD), .clk(CLOCK), .Q(L3), .clr(RESET));
  Register #(.width(1)) register_5 (.D(I4), .en(LOAD), .clk(CLOCK), .Q(L4), .clr(RESET));
  Register #(.width(1)) register_6 (.D(I5), .en(LOAD), .clk(CLOCK), .Q(L5), .clr(RESET));
  Register #(.width(1)) register_7 (.D(I6), .en(LOAD), .clk(CLOCK), .Q(L6), .clr(RESET));
  Register #(.width(1)) register_8 (.D(I7), .en(LOAD), .clk(CLOCK), .Q(L7), .clr(RESET));
  assign O6 = ENABLE ? L6 : 1'bz;  // Controlled_Buffer controlled_buffer_1
  assign O7 = ENABLE ? L7 : 1'bz;  // Controlled_Buffer controlled_buffer_2
  assign O2 = ENABLE ? L2 : 1'bz;  // Controlled_Buffer controlled_buffer_3
  assign O3 = ENABLE ? L3 : 1'bz;  // Controlled_Buffer controlled_buffer_4
  assign O4 = ENABLE ? L4 : 1'bz;  // Controlled_Buffer controlled_buffer_5
  assign O5 = ENABLE ? L5 : 1'bz;  // Controlled_Buffer controlled_buffer_6
  assign O0 = ENABLE ? L0 : 1'bz;  // Controlled_Buffer controlled_buffer_7
  assign O1 = ENABLE ? L1 : 1'bz;  // Controlled_Buffer controlled_buffer_8
endmodule

module registro_8bits_test (
  input  in_1,
  input  in_2,
  input  in_3,
  input  in_4,
  input  in_5,
  input  in_6,
  input  in_7,
  input  in_8,
  input  in_9,
  input  in_10,
  input  in_11,
  input  in_12,
  input  in_13,
  input  in_14,
  input  in_15,
  input  in_16,
  input  in_17
);

  wire alu_1_l0, alu_1_l1, alu_1_l2, alu_1_l3, alu_1_l4, alu_1_l5, alu_1_l6, alu_1_l7, clock_1_out,
       controlled_buffer_1_out, controlled_buffer_2_out, controlled_buffer_3_out, controlled_buffer_4_out,
       controlled_buffer_5_out, controlled_buffer_6_out, controlled_buffer_7_out, controlled_buffer_8_out,
       registro_8bit_1_l0, registro_8bit_1_l1, registro_8bit_1_l2, registro_8bit_1_l3, registro_8bit_1_l4,
       registro_8bit_1_l5, registro_8bit_1_l6, registro_8bit_1_l7, registro_8bits_b_1_l0,
       registro_8bits_b_1_l1, registro_8bits_b_1_l2, registro_8bits_b_1_l3, registro_8bits_b_1_l4,
       registro_8bits_b_1_l5, registro_8bits_b_1_l6, registro_8bits_b_1_l7;

  assign controlled_buffer_1_out = in_1 ? in_9 : 1'bz;  // Controlled_Buffer controlled_buffer_1
  assign controlled_buffer_2_out = in_1 ? in_8 : 1'bz;  // Controlled_Buffer controlled_buffer_2
  assign controlled_buffer_3_out = in_1 ? in_7 : 1'bz;  // Controlled_Buffer controlled_buffer_3
  assign controlled_buffer_4_out = in_1 ? in_6 : 1'bz;  // Controlled_Buffer controlled_buffer_4
  assign controlled_buffer_5_out = in_1 ? in_5 : 1'bz;  // Controlled_Buffer controlled_buffer_5
  assign controlled_buffer_6_out = in_1 ? in_4 : 1'bz;  // Controlled_Buffer controlled_buffer_6
  assign controlled_buffer_7_out = in_1 ? in_3 : 1'bz;  // Controlled_Buffer controlled_buffer_7
  assign controlled_buffer_8_out = in_1 ? in_2 : 1'bz;  // Controlled_Buffer controlled_buffer_8
  DotMatrix #(.dotshape("circle"), .matrixcols(8), .matrixrows(1)) dotmatrix_1 (
    .col0(controlled_buffer_8_out), .col1(controlled_buffer_7_out), .col2(controlled_buffer_6_out),
    .col3(controlled_buffer_5_out), .col4(controlled_buffer_4_out), .col5(controlled_buffer_3_out),
    .col6(controlled_buffer_2_out), .col7(controlled_buffer_1_out));
  DotMatrix #(.matrixcols(8), .matrixrows(1)) dotmatrix_2 (
    .col0(registro_8bit_1_l0), .col1(registro_8bit_1_l1), .col2(registro_8bit_1_l2),
    .col3(registro_8bit_1_l3), .col4(registro_8bit_1_l4), .col5(registro_8bit_1_l5),
    .col6(registro_8bit_1_l6), .col7(registro_8bit_1_l7));
  DotMatrix #(.matrixcols(8), .matrixrows(1)) dotmatrix_3 (
    .col0(registro_8bits_b_1_l0), .col1(registro_8bits_b_1_l1), .col2(registro_8bits_b_1_l2),
    .col3(registro_8bits_b_1_l3), .col4(registro_8bits_b_1_l4), .col5(registro_8bits_b_1_l5),
    .col6(registro_8bits_b_1_l6), .col7(registro_8bits_b_1_l7));
  registro_8bit registro_8bit_1 (
    .ENABLE(in_12), .I0(controlled_buffer_1_out), .I1(controlled_buffer_2_out), .I2(controlled_buffer_3_out),
    .I3(controlled_buffer_4_out), .I4(controlled_buffer_5_out), .I5(controlled_buffer_6_out),
    .I6(controlled_buffer_7_out), .I7(controlled_buffer_8_out), .CLOCK(clock_1_out), .LOAD(in_11),
    .RESET(in_10), .O0(controlled_buffer_1_out), .O1(controlled_buffer_2_out), .O2(controlled_buffer_3_out),
    .O3(controlled_buffer_4_out), .O4(controlled_buffer_5_out), .O5(controlled_buffer_6_out),
    .O6(controlled_buffer_7_out), .O7(controlled_buffer_8_out), .L0(registro_8bit_1_l0),
    .L1(registro_8bit_1_l1), .L2(registro_8bit_1_l2), .L3(registro_8bit_1_l3), .L4(registro_8bit_1_l4),
    .L5(registro_8bit_1_l5), .L6(registro_8bit_1_l6), .L7(registro_8bit_1_l7));
  registro_8bits_B registro_8bits_b_1 (
    .ENABLE(in_17), .I0(controlled_buffer_1_out), .I1(controlled_buffer_2_out), .I2(controlled_buffer_3_out),
    .I3(controlled_buffer_4_out), .I4(controlled_buffer_5_out), .I5(controlled_buffer_6_out),
    .I6(controlled_buffer_7_out), .I7(controlled_buffer_8_out), .CLOCK(clock_1_out), .LOAD(in_16),
    .RESET(in_15), .O0(controlled_buffer_1_out), .O1(controlled_buffer_2_out), .O2(controlled_buffer_3_out),
    .O3(controlled_buffer_4_out), .O4(controlled_buffer_5_out), .O5(controlled_buffer_6_out),
    .O6(controlled_buffer_7_out), .O7(controlled_buffer_8_out), .L0(registro_8bits_b_1_l0),
    .L1(registro_8bits_b_1_l1), .L2(registro_8bits_b_1_l2), .L3(registro_8bits_b_1_l3),
    .L4(registro_8bits_b_1_l4), .L5(registro_8bits_b_1_l5), .L6(registro_8bits_b_1_l6),
    .L7(registro_8bits_b_1_l7));
  DotMatrix #(.matrixcols(8), .matrixrows(1)) dotmatrix_4 (
    .col0(alu_1_l0), .col1(alu_1_l1), .col2(alu_1_l2), .col3(alu_1_l3), .col4(alu_1_l4), .col5(alu_1_l5),
    .col6(alu_1_l6), .col7(alu_1_l7));
  ALU alu_1 (
    .ENABLE(in_13), .A7(registro_8bit_1_l7), .B7(registro_8bits_b_1_l7), .A6(registro_8bit_1_l6),
    .B6(registro_8bits_b_1_l6), .A5(registro_8bit_1_l5), .B5(registro_8bits_b_1_l5), .A4(registro_8bit_1_l4),
    .B4(registro_8bits_b_1_l4), .A3(registro_8bit_1_l3), .B3(registro_8bits_b_1_l3), .A2(registro_8bit_1_l2),
    .B2(registro_8bits_b_1_l2), .A1(registro_8bit_1_l1), .B1(registro_8bits_b_1_l1), .A0(registro_8bit_1_l0),
    .B0(registro_8bits_b_1_l0), .su(in_14), .E0(controlled_buffer_1_out), .E1(controlled_buffer_2_out),
    .E2(controlled_buffer_3_out), .E3(controlled_buffer_4_out), .E4(controlled_buffer_5_out),
    .E5(controlled_buffer_6_out), .E6(controlled_buffer_7_out), .E7(controlled_buffer_8_out), .L7(alu_1_l7),
    .L6(alu_1_l6), .L5(alu_1_l5), .L4(alu_1_l4), .L3(alu_1_l3), .L2(alu_1_l2), .L1(alu_1_l1), .L0(alu_1_l0));  // open: CF, ZF
  Clock clock_1 (.out(clock_1_out));
endmodule

module ALU (
  input  ENABLE,
  input  su,
  input  A7,
  input  A6,
  input  A5,
  input  A4,
  input  A3,
  input  A2,
  input  A1,
  input  A0,
  input  B7,
  input  B6,
  input  B5,
  input  B4,
  input  B3,
  input  B2,
  input  B1,
  input  B0,
  output L7,
  output L6,
  output L5,
  output L4,
  output L3,
  output L2,
  output L1,
  output L0,
  output E0,
  output CF,
  output ZF,
  output E1,
  output E2,
  output E3,
  output E4,
  output E5,
  output E6,
  output E7
);

  wire [7:0] xor_8_out;

  xor xor_1 (xor_8_out[7], B7, su);
  xor xor_2 (xor_8_out[6], B6, su);
  xor xor_3 (xor_8_out[5], B5, su);
  Adder adder_1 (
    .a({A7, A6, A5, A4, A3, A2, A1, A0}), .b(xor_8_out), .out({L7, L6, L5, L4, L3, L2, L1, L0}), .cin(su),
    .cout(CF));
  xor xor_4 (xor_8_out[4], B4, su);
  xor xor_5 (xor_8_out[3], B3, su);
  xor xor_6 (xor_8_out[2], B2, su);
  xor xor_7 (xor_8_out[1], B1, su);
  xor xor_8 (xor_8_out[0], B0, su);
  nor nor_1 (ZF, L0, L1, L2, L3, L4, L5, L6, L7);
  assign E0 = ENABLE ? L0 : 1'bz;  // Controlled_Buffer controlled_buffer_1
  assign E1 = ENABLE ? L1 : 1'bz;  // Controlled_Buffer controlled_buffer_2
  assign E2 = ENABLE ? L2 : 1'bz;  // Controlled_Buffer controlled_buffer_3
  assign E3 = ENABLE ? L3 : 1'bz;  // Controlled_Buffer controlled_buffer_4
  assign E4 = ENABLE ? L4 : 1'bz;  // Controlled_Buffer controlled_buffer_5
  assign E5 = ENABLE ? L5 : 1'bz;  // Controlled_Buffer controlled_buffer_6
  assign E6 = ENABLE ? L6 : 1'bz;  // Controlled_Buffer controlled_buffer_7
  assign E7 = ENABLE ? L7 : 1'bz;  // Controlled_Buffer controlled_buffer_8
endmodule

module registro_8bits_B (
  input  CLOCK,
  input  LOAD,
  input  RESET,
  input  ENABLE,
  input  I0,
  input  I1,
  input  I2,
  input  I3,
  input  I4,
  input  I5,
  input  I6,
  input  I7,
  output L0,
  output L1,
  output L2,
  output L3,
  output L4,
  output L5,
  output L6,
  output L7,
  output O0,
  output O1,
  output O2,
  output O3,
  output O4,
  output O5,
  output O6,
  output O7
);

  Register #(.width(1)) register_1 (.D(I0), .en(LOAD), .clk(CLOCK), .Q(L0), .clr(RESET));
  Register #(.width(1)) register_2 (.D(I1), .en(LOAD), .clk(CLOCK), .Q(L1), .clr(RESET));
  Register #(.width(1)) register_3 (.D(I2), .en(LOAD), .clk(CLOCK), .Q(L2), .clr(RESET));
  Register #(.width(1)) register_4 (.D(I3), .en(LOAD), .clk(CLOCK), .Q(L3), .clr(RESET));
  Register #(.width(1)) register_5 (.D(I4), .en(LOAD), .clk(CLOCK), .Q(L4), .clr(RESET));
  Register #(.width(1)) register_6 (.D(I5), .en(LOAD), .clk(CLOCK), .Q(L5), .clr(RESET));
  Register #(.width(1)) register_7 (.D(I6), .en(LOAD), .clk(CLOCK), .Q(L6), .clr(RESET));
  Register #(.width(1)) register_8 (.D(I7), .en(LOAD), .clk(CLOCK), .Q(L7), .clr(RESET));
  assign O6 = ENABLE ? L6 : 1'bz;  // Controlled_Buffer controlled_buffer_1
  assign O7 = ENABLE ? L7 : 1'bz;  // Controlled_Buffer controlled_buffer_2
  assign O2 = ENABLE ? L2 : 1'bz;  // Controlled_Buffer controlled_buffer_3
  assign O3 = ENABLE ? L3 : 1'bz;  // Controlled_Buffer controlled_buffer_4
  assign O4 = ENABLE ? L4 : 1'bz;  // Controlled_Buffer controlled_buffer_5
  assign O5 = ENABLE ? L5 : 1'bz;  // Controlled_Buffer controlled_buffer_6
  assign O0 = ENABLE ? L0 : 1'bz;  // Controlled_Buffer controlled_buffer_7
  assign O1 = ENABLE ? L1 : 1'bz;  // Controlled_Buffer controlled_buffer_8
endmodule
